// Logisim project p2_final.circ as structural Verilog: 25 circuits, main circuit MIPS32
module MIPS32 (
);

  wire and_1_out, clock_1_out, decode_1_immunsig, decode_1_isword, decode_1_jtype, decode_1_regwr,
       decode_1_unsiglb, execute_1_bt, execute_1_j, execute_1_regwro, exme_1_iswordo, exme_1_memreado,
       exme_1_memtorego, exme_1_memwriteo, exme_1_regwro, exme_1_ulbo, idex_1_iswordo, idex_1_jtypeo,
       idex_1_regwro, idex_1_ulbo, ifid_1_delayo, loadstall_1_stall, memcmp_1_memwo, mewb_1_memtorego,
       multiplexer_5_out, not_1_out, or_1_out, registerfile_1_p3;
  wire [1:0] forwardingunit_1_forwarda, forwardingunit_1_forwardb, memcmp_1_re;
  wire [3:0] memcmp_1_sel;
  wire [4:0] bit_extender_1_out, exme_1_rdo, idex_1_rdo, idex_1_rso, idex_1_rto, idex_1_shamto,
       multiplexer_1_out_2, multiplexer_1_out_3, multiplexer_3_out, multiplexer_6_out, multiplexer_7_out,
       multiplexer_8_out, registerfile_1_p4, RThirtyOne;
  wire [6:0] decode_1_br_op, idex_1_br_opo;
  wire [7:0] multiplexer_9_out;
  wire [15:0] multiplexer_1_out;
  wire [17:0] decode_1_controls, idex_1_conto, multiplexer_4_out, nopc_1_nopc;
  wire [23:0] memcmp_1_a;
  wire [25:0] idex_1_targeto;
  wire [31:0] adder_1_out, bit_extender_3_out, bit_extender_4_out, bit_extender_5_out, bit_extender_6_out,
       execute_1_addr, execute_1_c, execute_1_jumpt, exme_1_addro, exme_1_co, fetch_1_addr, idex_1_ao,
       idex_1_bo, idex_1_immo, idex_1_pcfouro, ifid_1_instrout, ifid_1_pcfouro, memcmp_1_d, mewb_1_co,
       mewb_1_memdo, mips_ram_1_p7, mipsprogramrom_1_p2, multiplexer_2_out, multiplexer_10_out,
       multiplexer_11_out, nop, plusfour_1_pcfour, registerfile_1_p1, registerfile_1_p7, registerfile_1_p8,
       shifttwo_1_out_3;
  wire [31:26] multiplexer_1_out_4;

  Clock clock_1 (.out(clock_1_out));
  Fetch fetch_1 (
    .jump(execute_1_j), .Stall(loadstall_1_stall), .jumpT(execute_1_jumpt), .Clk(clock_1_out),
    .bt(execute_1_bt), .b_target(adder_1_out), .Addr(fetch_1_addr));
  plusfour plusfour_1 (.PC(fetch_1_addr), .PCFour(plusfour_1_pcfour));
  or or_1 (or_1_out, execute_1_j, execute_1_bt);
  // MIPSProgramROM mipsprogramrom_1: pin names not known; wires that end beside it: fetch_1_addr, mipsprogramrom_1_p2
  IFID ifid_1 (
    .instrOut(ifid_1_instrout), .instrn(mipsprogramrom_1_p2), .Clk(clock_1_out), .PCFourO(ifid_1_pcfouro),
    .PCFour(plusfour_1_pcfour), .Delay(or_1_out), .DelayO(ifid_1_delayo), .Stall(loadstall_1_stall));
  not not_1 (not_1_out, clock_1_out);
  Multiplexer #(.width(32), .enable("false")) multiplexer_1 (
    .in0(ifid_1_instrout), .in1(nop),
    .out({multiplexer_1_out_4, multiplexer_1_out_3, multiplexer_1_out_2, multiplexer_1_out}),
    .sel(ifid_1_delayo));
  assign bit_extender_1_out = {{4{1'b0}}, multiplexer_1_out_4[30]};  // Bit_Extender bit_extender_1
  assign nop = {{31{multiplexer_1_out_4[30]}}, multiplexer_1_out_4[30]};  // Bit_Extender bit_extender_2
  LoadStall loadstall_1 (
    .EX_memR(idex_1_conto[13]), .ID_rs(multiplexer_1_out_3), .EX_rd(idex_1_rdo), .ID_rt(multiplexer_1_out_2),
    .stall(loadstall_1_stall));
  assign bit_extender_3_out = {{16{multiplexer_1_out[15]}}, multiplexer_1_out};  // Bit_Extender bit_extender_3
  assign bit_extender_4_out = {{16{1'b0}}, multiplexer_1_out};  // Bit_Extender bit_extender_4
  // RegisterFile registerfile_1: pin names not known; wires that end beside it: registerfile_1_p1, not_1_out, registerfile_1_p3, registerfile_1_p4, multiplexer_1_out_3, multiplexer_1_out_2, registerfile_1_p7, registerfile_1_p8
  Multiplexer #(.width(32), .enable("false")) multiplexer_2 (
    .in0(bit_extender_3_out), .in1(bit_extender_4_out), .out(multiplexer_2_out), .sel(decode_1_immunsig));
  assign RThirtyOne = ~bit_extender_1_out;  // NOT_Gate not_2, 5 bits wide
  nopC nopc_1 (.nopC(nopc_1_nopc), .zIn(multiplexer_1_out_4[30]));
  Decode decode_1 (
    .instr({multiplexer_1_out_4, multiplexer_1_out_3, multiplexer_1_out_2, multiplexer_1_out}),
    .regWr(decode_1_regwr), .immunsig(decode_1_immunsig), .controls(decode_1_controls),
    .br_op(decode_1_br_op), .jtype(decode_1_jtype), .unsigLB(decode_1_unsiglb), .isWord(decode_1_isword));
  Multiplexer #(.width(5), .enable("false")) multiplexer_3 (
    .in0(multiplexer_1_out_2), .in1(multiplexer_1_out[15:11]), .out(multiplexer_3_out),
    .sel(decode_1_controls[4]));
  Multiplexer #(.width(18), .enable("false")) multiplexer_4 (
    .in0(decode_1_controls), .in1(nopc_1_nopc), .out(multiplexer_4_out), .sel(loadstall_1_stall));
  Multiplexer #(.enable("false")) multiplexer_5 (
    .in0(decode_1_regwr), .in1(multiplexer_1_out_4[30]), .out(multiplexer_5_out), .sel(loadstall_1_stall));
  Multiplexer #(.width(5), .enable("false")) multiplexer_6 (
    .in0(bit_extender_1_out), .in1(multiplexer_1_out_2), .out(multiplexer_6_out), .sel(decode_1_controls[4]));
  Multiplexer #(.width(5), .enable("false")) multiplexer_7 (
    .in0(multiplexer_6_out), .in1(multiplexer_1_out_2), .out(multiplexer_7_out), .sel(decode_1_controls[14]));
  IDEX idex_1 (
    .A(registerfile_1_p7), .AO(idex_1_ao), .B(registerfile_1_p8), .BO(idex_1_bo), .Clk(clock_1_out),
    .rd(multiplexer_3_out), .rdO(idex_1_rdo), .rt(multiplexer_7_out), .rtO(idex_1_rto),
    .shamt(multiplexer_1_out[10:6]), .shamtO(idex_1_shamto), .Imm(multiplexer_2_out), .ImmO(idex_1_immo),
    .rs(multiplexer_1_out_3), .rsO(idex_1_rso), .cont(multiplexer_4_out), .contO(idex_1_conto),
    .regWrO(idex_1_regwro), .regWr(multiplexer_5_out), .br_op(decode_1_br_op), .br_opO(idex_1_br_opo),
    .PCFour(ifid_1_pcfouro), .PCFourO(idex_1_pcfouro), .jtype(decode_1_jtype), .jtypeO(idex_1_jtypeo),
    .target({multiplexer_1_out_3, multiplexer_1_out_2, multiplexer_1_out}), .targetO(idex_1_targeto),
    .isWord(decode_1_isword), .ULB(decode_1_unsiglb), .isWordO(idex_1_iswordo), .ULBO(idex_1_ulbo));
  shifttwo shifttwo_1 (.z(idex_1_conto[13]), .imm(idex_1_immo), .out_3(shifttwo_1_out_3));
  Adder #(.width(32)) adder_1 (.a(idex_1_pcfouro), .b(shifttwo_1_out_3), .out(adder_1_out));  // open: cin, cout
  and and_1 (and_1_out, idex_1_jtypeo, idex_1_conto[16]);
  Execute execute_1 (
    .C(execute_1_c), .A(idex_1_ao), .B(idex_1_bo), .imm(idex_1_immo), .shamt(idex_1_shamto),
    .controls(idex_1_conto), .regWrO(execute_1_regwro), .regWr(idex_1_regwro),
    .ForwardA(forwardingunit_1_forwarda), .ForwardB(forwardingunit_1_forwardb), .EXMEMC(exme_1_co),
    .MEMWBC(registerfile_1_p1), .bt(execute_1_bt), .br_op(idex_1_br_opo), .jtype(idex_1_jtypeo),
    .target(idex_1_targeto), .pc4(idex_1_pcfouro), .jumpT(execute_1_jumpt), .j(execute_1_j),
    .Addr(execute_1_addr));
  ForwardingUnit forwardingunit_1 (
    .EM_regWr(exme_1_regwro), .EM_rd(exme_1_rdo), .IE_rs(idex_1_rso), .IE_rt(idex_1_rto),
    .MW_regWr(registerfile_1_p3), .MW_rd(registerfile_1_p4), .ForwardA(forwardingunit_1_forwarda),
    .ForwardB(forwardingunit_1_forwardb));
  Multiplexer #(.width(5), .enable("false")) multiplexer_8 (
    .in0(idex_1_rdo), .in1(RThirtyOne), .out(multiplexer_8_out), .sel(and_1_out));
  EXME exme_1 (
    .rdO(exme_1_rdo), .RegWrO(exme_1_regwro), .Clk(clock_1_out), .MemtoRegO(exme_1_memtorego),
    .C(execute_1_c), .controls(idex_1_conto), .CO(exme_1_co), .rd(multiplexer_8_out),
    .MemReadO(exme_1_memreado), .MemWriteO(exme_1_memwriteo), .RegWr(execute_1_regwro),
    .isWord(idex_1_iswordo), .ULB(idex_1_ulbo), .isWordO(exme_1_iswordo), .ULBO(exme_1_ulbo),
    .AddrO(exme_1_addro), .Addr(execute_1_addr));
  MemCmp memcmp_1 (
    .C(exme_1_co), .Addr(exme_1_addro), .isWord(exme_1_iswordo), .MemW(exme_1_memwriteo), .D(memcmp_1_d),
    .Re(memcmp_1_re), .sel(memcmp_1_sel), .A(memcmp_1_a), .MemWO(memcmp_1_memwo));
  // MIPS_RAM #(.addrWidth(24)) mips_ram_1: pin names not known; wires that end beside it: memcmp_1_a, memcmp_1_d, memcmp_1_memwo, memcmp_1_sel, clock_1_out, exme_1_memreado, mips_ram_1_p7
  assign bit_extender_5_out = {{24{multiplexer_9_out[7]}}, multiplexer_9_out};  // Bit_Extender bit_extender_5
  Multiplexer #(.select(2), .width(8), .enable("false")) multiplexer_9 (
    .in0(mips_ram_1_p7[7:0]), .in1(mips_ram_1_p7[15:8]), .in2(mips_ram_1_p7[23:16]),
    .in3(mips_ram_1_p7[31:24]), .out(multiplexer_9_out), .sel(memcmp_1_re));
  assign bit_extender_6_out = {{24{1'b0}}, multiplexer_9_out};  // Bit_Extender bit_extender_6
  Multiplexer #(.width(32), .enable("false")) multiplexer_10 (
    .in0(bit_extender_5_out), .in1(bit_extender_6_out), .out(multiplexer_10_out), .sel(exme_1_ulbo));
  Multiplexer #(.width(32), .enable("false")) multiplexer_11 (
    .in0(multiplexer_10_out), .in1(mips_ram_1_p7), .out(multiplexer_11_out), .sel(exme_1_iswordo));
  MEWB mewb_1 (
    .regWrtO(registerfile_1_p3), .rdO(registerfile_1_p4), .C(exme_1_co), .Clk(clock_1_out), .rd(exme_1_rdo),
    .regWrt(exme_1_regwro), .CO(mewb_1_co), .MemtoReg(exme_1_memtorego), .MemtoRegO(mewb_1_memtorego),
    .MemD(multiplexer_11_out), .MemDO(mewb_1_memdo));
  Multiplexer #(.width(32), .enable("false")) multiplexer_12 (
    .in0(mewb_1_co), .in1(mewb_1_memdo), .out(registerfile_1_p1), .sel(mewb_1_memtorego));

  // Notes on the sheet:
  //   contents of mipsprogramrom_1 (hex, n*v repeats v):
  //   addiu $2, $0, 1 addiu $3, $0, 0 addiu $4, $0, 1 xori $19, $18, 6 movn $6, $18, $9 movz $11, $10, $9
  //   slti $20, $4, 5 sltiu $6, $4, 1 addu $3, $2, $1 subu $3, $2, $1 and $5, $5, $5 addiu $5, $0, 2 addiu
  //   $6, $0, -4 addiu $7, $0, 8 movn $1, $17, $9 movz $4, $16, $9 addiu $8, $0, 6 addiu $9, $0, 6 xori
  //   $19, $8, 6 slti $25, $4, 5 sltiu $3, $4, 1 addu $3, $2, $1 subu $3, $2, $1 and $5, $5, $5 addiu $10,
  //   $0,9 addiu $11, $0, 10 addiu $12, $0, 30 addiu $13, $0, 4 addiu $14, $0, 3 xori $11, $18, 6 slti
  //   $22, $3, 52 sltiu $3, $4, 14 addu $3, $2, $1 subu $3, $2, $1 and $5, $5, $5 addiu $15, $0, 2 addiu
  //   $16, $0, 1 addiu $17, $0, 9 addiu $7, $0, 4 addiu $18, $0, 0 addiu $19, $0, 1 andi $19, $18, 8 ori
  //   $19, $18, 7 xori $19, $18, 6 slti $21, $2, 5 sltiu $6, $4, 1 addu $3, $2, $1 subu $3, $2, $1 and $5,
  //   $5, $5 or $5, $5, $5 xor $22, $4, $4 nor $24, $3, $5 slt $4, $6, $5 sltu $18, $23, $12 movn $11,
  //   $10, $9 movz $11, $10, $9 sll $1, $2, 8 srl $1, $1, 9 sra $1, $1, 5 sllv $3, $1, $5 srlv $2, $3, $6
  //   srav $3, $5, $8 lui $5, 24 lui $24, 28 j THIS addiu $4, $4, 4 jr $7 andi $13, $15, 22 jal CLASS ori
  //   $20, $21, 22 jalr $30, $7 xori $21, $22, 100 bgez $4, CLASS lw $2, 2($29) lb $3, 0($29) or $20, $3,
  //   $22 addiu $1, $0, 5 addiu $2, $0, 6 addiu $3, $0, 2 beq $3, $4, SUCKS slti $9, $4, 1 bne $2, $3,
  //   SUCKS sltiu $5, $6, 1 blez $15, THIS addu $12, $13, $14 bgtz $12, CLASS subu $20, $2, $2 bltz $5,
  //   SUCKS and $1, $1, $2 bgez $4, CLASS or $20, $3, $22 blez $15, DEATH addu $12, $13, $14 bgtz $12, BYE
  //   subu $20, $2, $2 bltz $5, SUCKS and $1, $1, $2 bgez $4, FOREVER or $20, $3, $22  #define stack
  //   pointer! addiu $29, $29, 32000  lw $20, 0($29) xor $4, $6, $12 lw $21, 2($29) nor $13, $21, $15 lbu
  //   $22, 4($29) lbu $23, 2($29) lbu $24, 0($29) slt $5, $5, $5 sw $2, 5($29) sltu $6, $6, $6 sb $21,
  //   0($29) lw $20, 2($29) lw $21, 3($29) lw $22, 4($29) movn $3, $13, $16 movz $2, $14, $10 sll $2, $2,
  //   10 j BYE srl $3, $16, 17 j FOREVER srl $17, $5, 10 j THIS sra $4, $5, 3 jal SUCKS sllv $2, $3, $4
  //   jal FOREVER srlv $5, $8, $9 jalr $5, $7 srav $3, $8, $14 jalr $4, $13 lui $4, 33 jalr $4, $7 lw $20,
  //   6($29) lw $21, 4($29) lw $22, 2($29) lb $23, 0($29) lb $24, 3($29) lbu $25, 0($29) lbu $25, 5($29)
  //   lbu $25, 3($29) bne $3, $3, SUCKS sltiu $9, $5, 1 blez $5, THIS addu $6, $6, $5 sw $2, 0($29) sw $3,
  //   2($29) sw $4, 3($29) sb $4, 2($29) sb $5, 1($29) sb $6, 0($29) bgtz $12, CLASS lbu $25, 5($29) lbu
  //   $25, 3($29) subu $20, $2, $2 bltz $5, SUCKS and $1, $1, $2 bgez $4, CLASS lw $22, 2($29) lb $23,
  //   0($29) or $20, $3, $22 blez $15, DEATH addiu $4, $0, -22 sb $4, 2($29) lb $2, 2($29) lbu $2, 2($29)
  //   lb $23, 2($29) lbu $22, 6($29) slt $0, $0, $0 sb $4, 2($29) lb $2, 2($29) lbu $3, 2($29)  THIS:
  //   sltiu $6, $4, 1 addu $3, $2, $1 subu $3, $2, $1 and $5, $5, $5 or $5, $5, $5   CLASS: sllv $21, $1,
  //   $5 srlv $21, $3, $6 srav $25, $21, $8  SUCKS: addiu $11, $2, 12 addiu $14, $0, 6 addiu $16, $0, 2
  //   WHYY: xor $10, $9, $8 addiu $26, $0, 26  BYE: ori $20, $21, 22 xori $21, $22, 23 addiu $1, $0, 5
  //   addiu $2, $0, 6  FOREVER: ori $19, $18, 7 xori $19, $18, 6 slti $20, $4, 5 sltiu $6, $4, 1 addu $3,
  //   $2, $1  DEATH: slti $9, $4, 1 sltiu $8, $6, 1
endmodule

module IFID (
  input  Stall,
  input  [31:0] instrn,
  input  [31:0] PCFour,
  input  Delay,
  input  Clk,
  output [31:0] instrOut,
  output [31:0] PCFourO,
  output DelayO
);

  wire not_1_out, not_2_out;

  not not_1 (not_1_out, Stall);
  not not_2 (not_2_out, Stall);
  Register #(.width(32)) register_1 (.D(instrn), .en(not_1_out), .clk(Clk), .Q(instrOut));  // open: clr
  Register #(.width(32)) register_2 (.D(PCFour), .en(not_2_out), .clk(Clk), .Q(PCFourO));  // open: clr
  Register #(.width(1)) register_3 (.D(Delay), .clk(Clk), .Q(DelayO));  // open: en, clr
endmodule

module IDecode (
  input  [31:0] instr,
  output [17:0] controls,
  output memWr,
  output br,
  output [6:0] br_op,
  output unsigLB,
  output isWord
);

  wire and_1_out, and_2_out, and_5_out, and_6_out, and_7_out, and_8_out, and_9_out, and_10_out, and_11_out,
       and_12_out, and_13_out, and_15_out, not_1_out, not_2_out, not_3_out, not_4_out, not_5_out, not_6_out,
       not_7_out, not_8_out, not_9_out, not_10_out, not_11_out, not_12_out, not_13_out, not_14_out,
       not_15_out, not_16_out, not_17_out, not_18_out, not_19_out, not_20_out, not_21_out, not_22_out,
       not_23_out, not_24_out, not_25_out, not_26_out, not_27_out, not_28_out, not_29_out, not_30_out,
       not_31_out, not_32_out, not_33_out, not_34_out, not_35_out, not_36_out, or_1_out, or_2_out, or_3_out;
  wire [7:7] multiplexer_1_out;
  wire [10:0] or_4_out;
  wire [15:0] memdecode_1_alu3;

  not not_1 (not_1_out, instr[31]);
  not not_2 (not_2_out, instr[30]);
  not not_3 (not_3_out, instr[29]);
  and and_1 (and_1_out, not_1_out, not_2_out, not_3_out, instr[28], not_4_out, not_5_out);
  not not_4 (not_4_out, instr[27]);
  not not_5 (not_5_out, instr[26]);
  not not_6 (not_6_out, instr[31]);
  not not_7 (not_7_out, instr[30]);
  not not_8 (not_8_out, instr[29]);
  and and_2 (and_2_out, not_6_out, not_7_out, not_8_out, instr[28], not_9_out, instr[26]);
  not not_9 (not_9_out, instr[27]);
  not not_10 (not_10_out, instr[31]);
  not not_11 (not_11_out, instr[30]);
  not not_12 (not_12_out, instr[28]);
  Branch branch_1 (.instr(instr), .branch(br), .b_op(br_op));
  MemDecode memdecode_1 (
    .op(instr[31:26]), .ALU3(memdecode_1_alu3[0]), .ALU2(memdecode_1_alu3[1]), .ALU1(memdecode_1_alu3[2]),
    .ALU0(memdecode_1_alu3[3]), .RegDst(memdecode_1_alu3[4]), .ALUSrc(memdecode_1_alu3[5]),
    .MemtoReg(memdecode_1_alu3[6]), .RegWrite(memdecode_1_alu3[7]), .MemRead(memdecode_1_alu3[8]),
    .MemWrite(memWr), .ALUOut(memdecode_1_alu3[10]), .unsigLB(unsigLB), .isWord(isWord));
  and and_3 (memdecode_1_alu3[14], not_10_out, not_11_out, instr[29], not_12_out, instr[27], instr[26]);
  not not_13 (not_13_out, instr[31]);
  not not_14 (not_14_out, instr[30]);
  not not_15 (not_15_out, instr[31]);
  not not_16 (not_16_out, instr[29]);
  not not_17 (not_17_out, instr[28]);
  not not_18 (not_18_out, instr[26]);
  not not_19 (not_19_out, instr[31]);
  not not_20 (not_20_out, instr[29]);
  not not_21 (not_21_out, instr[31]);
  not not_22 (not_22_out, instr[28]);
  not not_23 (not_23_out, instr[26]);
  not not_24 (not_24_out, instr[29]);
  not not_25 (not_25_out, instr[27]);
  or or_1 (or_1_out, and_1_out, and_2_out);
  not not_26 (not_26_out, instr[27]);
  not not_27 (not_27_out, instr[31]);
  not not_28 (not_28_out, instr[27]);
  and and_4 (memdecode_1_alu3[15], not_13_out, not_14_out, instr[29], instr[28], instr[27], instr[26]);
  and and_5 (and_5_out, not_15_out, not_16_out, not_17_out, not_18_out);
  and and_6 (and_6_out, instr[29], instr[28], not_29_out);
  not not_29 (not_29_out, instr[27]);
  and and_7 (and_7_out, instr[29], instr[28], not_30_out);
  not not_30 (not_30_out, instr[26]);
  and and_8 (and_8_out, not_19_out, not_20_out);
  and and_9 (and_9_out, not_21_out, not_22_out, instr[27]);
  and and_10 (and_10_out, instr[27], not_23_out);
  and and_11 (and_11_out, not_24_out, instr[28], instr[27]);
  not not_31 (not_31_out, instr[29]);
  not not_32 (not_32_out, instr[28]);
  and and_12 (and_12_out, not_25_out, instr[26]);
  or or_2 (or_2_out, not_26_out, instr[28], instr[29], instr[31]);
  and and_13 (and_13_out, not_27_out, instr[29]);
  or or_3 (or_3_out, not_28_out, instr[28], instr[31]);
  or or_4 (or_4_out[0], and_5_out, and_6_out, and_7_out);
  or or_5 (or_4_out[1], and_8_out, and_9_out, and_10_out, and_11_out);
  or or_6 (or_4_out[2], not_31_out, not_32_out, and_12_out);
  not not_33 (not_33_out, or_1_out);
  not not_34 (not_34_out, br);
  and and_14 (or_4_out[5], not_33_out, or_2_out);
  and and_15 (and_15_out, or_3_out, not_34_out);
  not not_35 (not_35_out, br);
  not not_36 (not_36_out, br);
  and and_16 (or_4_out[7], and_13_out, not_35_out);
  and and_17 (or_4_out[10], and_15_out, not_36_out);
  Multiplexer #(.width(19), .enable("false")) multiplexer_1 (
    .in0({br, {2{instr[30]}}, memdecode_1_alu3[15:14], {3{instr[30]}}, or_4_out[10], {2{instr[30]}}, or_4_out[7], instr[30], or_4_out[5], instr[30], instr[31], or_4_out[2:0]}),
    .in1({br, {2{instr[30]}}, memdecode_1_alu3[15:14], {3{instr[30]}}, memdecode_1_alu3[10], memWr, memdecode_1_alu3[8:0]}),
    .out({controls[17:15], controls[11:6], controls[14:13], multiplexer_1_out[7], controls[12], controls[5:4], controls[0], controls[1], controls[2], controls[3]}),
    .sel(instr[31]));
endmodule

module Decode (
  input  [31:0] instr,
  output [17:0] controls,
  output [6:0] br_op,
  output regWr,
  output jtype,
  output immunsig,
  output unsigLB,
  output isWord
);

  wire and_2_out, and_3_out, idecode_1_br, idecode_1_memwr, jdecode_1_up31, multiplexer_3_out, nor_1_out,
       not_1_out, not_2_out, not_3_out, rdecode_1_j, rdecode_1_up31;
  wire [17:0] idecode_1_controls, jdecode_1_controls, multiplexer_1_out, rdecode_1_controls;

  nor nor_1 (nor_1_out, instr[26], instr[27], instr[28], instr[29], instr[30], instr[31]);
  not not_1 (not_1_out, nor_1_out);
  RDecode rdecode_1 (.funct(instr[5:0]), .controls(rdecode_1_controls), .j(rdecode_1_j), .up31(rdecode_1_up31));
  IDecode idecode_1 (
    .instr(instr), .controls(idecode_1_controls), .memWr(idecode_1_memwr), .br(idecode_1_br), .br_op(br_op),
    .unsigLB(unsigLB), .isWord(isWord));
  JDecode jdecode_1 (.op(instr[31:26]), .controls(jdecode_1_controls), .j(jtype), .up31(jdecode_1_up31));
  and and_1 (immunsig, not_1_out, instr[28], instr[29]);
  Multiplexer #(.width(18), .enable("false")) multiplexer_1 (
    .in0(idecode_1_controls), .in1(rdecode_1_controls), .out(multiplexer_1_out), .sel(nor_1_out));
  Multiplexer #(.width(18), .enable("false")) multiplexer_2 (
    .in0(multiplexer_1_out), .in1(jdecode_1_controls), .out(controls), .sel(jtype));
  not not_2 (not_2_out, rdecode_1_up31);
  not not_3 (not_3_out, jdecode_1_up31);
  and and_2 (and_2_out, not_2_out, rdecode_1_j);
  and and_3 (and_3_out, not_3_out, jtype);
  Multiplexer #(.enable("false")) multiplexer_3 (
    .in0(idecode_1_memwr), .in1(and_2_out), .out(multiplexer_3_out), .sel(nor_1_out));
  nor nor_2 (regWr, multiplexer_3_out, idecode_1_memwr, idecode_1_br, and_3_out);
endmodule

module IDEX (
  input  [31:0] A,
  input  [31:0] B,
  input  [4:0] rd,
  input  [4:0] rt,
  input  [4:0] shamt,
  input  [31:0] Imm,
  input  [4:0] rs,
  input  [17:0] cont,
  input  regWr,
  input  [6:0] br_op,
  input  [31:0] PCFour,
  input  isWord,
  input  ULB,
  input  jtype,
  input  [25:0] target,
  input  Clk,
  output [31:0] AO,
  output [31:0] BO,
  output [4:0] rdO,
  output [4:0] rtO,
  output [4:0] shamtO,
  output [31:0] ImmO,
  output [4:0] rsO,
  output [17:0] contO,
  output regWrO,
  output [6:0] br_opO,
  output [31:0] PCFourO,
  output isWordO,
  output ULBO,
  output jtypeO,
  output [25:0] targetO
);

  Register #(.width(32)) register_1 (.D(A), .clk(Clk), .Q(AO));  // open: en, clr
  Register #(.width(32)) register_2 (.D(B), .clk(Clk), .Q(BO));  // open: en, clr
  Register #(.width(5)) register_3 (.D(rd), .clk(Clk), .Q(rdO));  // open: en, clr
  Register #(.width(5)) register_4 (.D(rt), .clk(Clk), .Q(rtO));  // open: en, clr
  Register #(.width(5)) register_5 (.D(shamt), .clk(Clk), .Q(shamtO));  // open: en, clr
  Register #(.width(32)) register_6 (.D(Imm), .clk(Clk), .Q(ImmO));  // open: en, clr
  Register #(.width(5)) register_7 (.D(rs), .clk(Clk), .Q(rsO));  // open: en, clr
  Register #(.width(18)) register_8 (.D(cont), .clk(Clk), .Q(contO));  // open: en, clr
  Register #(.width(1)) register_9 (.D(regWr), .clk(Clk), .Q(regWrO));  // open: en, clr
  Register #(.width(7)) register_10 (.D(br_op), .clk(Clk), .Q(br_opO));  // open: en, clr
  Register #(.width(32)) register_11 (.D(PCFour), .clk(Clk), .Q(PCFourO));  // open: en, clr
  Register #(.width(1)) register_12 (.D(isWord), .clk(Clk), .Q(isWordO));  // open: en, clr
  Register #(.width(1)) register_13 (.D(ULB), .clk(Clk), .Q(ULBO));  // open: en, clr
  Register #(.width(1)) register_14 (.D(jtype), .clk(Clk), .Q(jtypeO));  // open: en, clr
  Register #(.width(26)) register_15 (.D(target), .clk(Clk), .Q(targetO));  // open: en, clr
endmodule

module Execute (
  input  [31:0] A,
  input  [6:0] br_op,
  input  [31:0] B,
  input  [31:0] MEMWBC,
  input  [31:0] imm,
  input  [31:0] EXMEMC,
  input  [4:0] shamt,
  input  [1:0] ForwardA,
  input  [1:0] ForwardB,
  input  regWr,
  input  [17:0] controls,
  input  jtype,
  input  [25:0] target,
  input  [31:0] pc4,
  output [31:0] C,
  output bt,
  output regWrO,
  output [31:0] jumpT,
  output j,
  output [31:0] Addr
);

  wire and_1_out, and_2_out, and_3_out, and_4_out, comparator_1_eq, comparator_1_lt, comparator_2_lt,
       not_1_out, not_2_out, or_1_out, or_2_out, xor_1_out;
  wire [4:0] mips_alu_1_p4, multiplexer_4_out;
  wire [31:0] bit_extender_1_out, bit_extender_2_out, bit_extender_3_out, mips_alu_1_p5, multiplexer_1_out,
       multiplexer_2_out, multiplexer_3_out, multiplexer_6_out, multiplexer_7_out, multiplexer_8_out,
       multiplexer_10_out, multiplexer_11_out, plusfour_1_pcfour;

  Multiplexer #(.width(32), .enable("false")) multiplexer_1 (
    .in0(B), .in1(imm), .out(multiplexer_1_out), .sel(xor_1_out));
  xor xor_1 (xor_1_out, controls[14], controls[5]);
  and and_1 (and_1_out, controls[15], controls[16]);
  Multiplexer #(.select(2), .width(32), .enable("false")) multiplexer_2 (
    .in0(A), .in1(MEMWBC), .in2(EXMEMC), .out(multiplexer_2_out), .sel(ForwardA));  // open: in3
  Multiplexer #(.select(2), .width(32), .enable("false")) multiplexer_3 (
    .in0(multiplexer_1_out), .in1(MEMWBC), .in2(EXMEMC), .out(multiplexer_3_out), .sel(ForwardB));  // open: in3
  assign bit_extender_1_out = {{31{1'b0}}, controls[12]};  // Bit_Extender bit_extender_1
  Multiplexer #(.width(5), .enable("false")) multiplexer_4 (
    .in0(shamt), .in1(multiplexer_2_out[4:0]), .out(multiplexer_4_out), .sel(controls[9]));
  jumpCmpt jumpcmpt_1 (
    .controls(controls), .jtype(jtype), .target(target), .plusfour(pc4), .rs(multiplexer_2_out), .newpc(jumpT));
  branchCmpt branchcmpt_1 (.controls(controls), .rs(multiplexer_2_out), .br_op(br_op), .rt(multiplexer_3_out), .br(bt));
  // Mips_ALU mips_alu_1: pin names not known; wires that end beside it: multiplexer_2_out, multiplexer_3_out, controls[3:0], mips_alu_1_p4, mips_alu_1_p5
  Multiplexer #(.width(5), .enable("false")) multiplexer_5 (
    .in0(multiplexer_4_out), .in1(5'b10000), .out(mips_alu_1_p4), .sel(controls[11]));
  Multiplexer #(.width(32), .enable("false")) multiplexer_6 (
    .in0(multiplexer_2_out), .in1(bit_extender_1_out), .out(multiplexer_6_out), .sel(controls[7]));
  Comparator #(.width(32)) comparator_1 (
    .a(multiplexer_6_out), .b(multiplexer_3_out), .eq(comparator_1_eq), .lt(comparator_1_lt));  // open: gt
  Comparator #(.width(32), .mode("unsigned")) comparator_2 (
    .a(multiplexer_2_out), .b(multiplexer_3_out), .lt(comparator_2_lt));  // open: gt, eq
  assign bit_extender_2_out = {{31{1'b0}}, comparator_2_lt};  // Bit_Extender bit_extender_2
  assign bit_extender_3_out = {{31{1'b0}}, comparator_1_lt};  // Bit_Extender bit_extender_3
  not not_1 (not_1_out, comparator_1_eq);
  not not_2 (not_2_out, controls[8]);
  and and_2 (and_2_out, not_1_out, controls[8]);
  and and_3 (and_3_out, comparator_1_eq, not_2_out);
  Multiplexer #(.width(32), .enable("false")) multiplexer_7 (
    .in0(bit_extender_2_out), .in1(mips_alu_1_p5), .out(multiplexer_7_out), .sel(controls[6]));
  Multiplexer #(.width(32), .enable("false")) multiplexer_8 (
    .in0(bit_extender_3_out), .in1(multiplexer_2_out), .out(multiplexer_8_out), .sel(controls[7]));
  Adder #(.width(32)) adder_1 (.a(imm), .b(multiplexer_2_out), .out(Addr));  // open: cin, cout
  or or_1 (or_1_out, and_2_out, and_3_out);
  plusfour plusfour_1 (.PC(pc4), .PCFour(plusfour_1_pcfour));
  Multiplexer #(.enable("false")) multiplexer_9 (.in0(regWr), .in1(and_4_out), .out(regWrO), .sel(controls[7]));
  and and_4 (and_4_out, controls[7], or_1_out);
  Multiplexer #(.width(32), .enable("false")) multiplexer_10 (
    .in0(multiplexer_8_out), .in1(multiplexer_7_out), .out(multiplexer_10_out), .sel(or_2_out));
  or or_2 (or_2_out, controls[10], controls[6]);
  Multiplexer #(.width(32), .enable("false")) multiplexer_11 (
    .in0(multiplexer_10_out), .in1(plusfour_1_pcfour), .out(multiplexer_11_out), .sel(and_1_out));
  Multiplexer #(.width(32), .enable("false")) multiplexer_12 (
    .in0(multiplexer_11_out), .in1(multiplexer_3_out), .out(C), .sel(controls[14]));

  assign j = controls[15];
endmodule

module EXME (
  input  [31:0] C,
  input  [4:0] rd,
  input  RegWr,
  input  [31:0] Addr,
  input  isWord,
  input  ULB,
  input  [17:0] controls,
  input  Clk,
  output [31:0] CO,
  output [4:0] rdO,
  output RegWrO,
  output [31:0] AddrO,
  output isWordO,
  output ULBO,
  output MemtoRegO,
  output MemReadO,
  output MemWriteO
);

  Register #(.width(32)) register_1 (.D(C), .clk(Clk), .Q(CO));  // open: en, clr
  Register #(.width(5)) register_2 (.D(rd), .clk(Clk), .Q(rdO));  // open: en, clr
  Register #(.width(1)) register_3 (.D(RegWr), .clk(Clk), .Q(RegWrO));  // open: en, clr
  Register #(.width(32)) register_4 (.D(Addr), .clk(Clk), .Q(AddrO));  // open: en, clr
  Register #(.width(1)) register_5 (.D(isWord), .clk(Clk), .Q(isWordO));  // open: en, clr
  Register #(.width(1)) register_6 (.D(ULB), .clk(Clk), .Q(ULBO));  // open: en, clr
  Register #(.width(1)) register_7 (.D(controls[12]), .clk(Clk), .Q(MemtoRegO));  // open: en, clr
  Register #(.width(1)) register_8 (.D(controls[13]), .clk(Clk), .Q(MemReadO));  // open: en, clr
  Register #(.width(1)) register_9 (.D(controls[14]), .clk(Clk), .Q(MemWriteO));  // open: en, clr
endmodule

module RDecode (
  input  [5:0] funct,
  output [17:0] controls,
  output j,
  output up31
);

  wire and_2_out, and_3_out, and_4_out, and_5_out, and_7_out, and_8_out, and_11_out, and_12_out, and_13_out,
       and_15_out, and_16_out, and_17_out, and_18_out, nor_1_out, not_1_out, not_2_out, not_3_out, not_4_out,
       not_5_out, not_6_out, not_7_out, not_8_out, not_9_out, not_11_out, not_12_out, not_13_out, not_14_out,
       not_15_out, not_16_out, not_17_out, not_18_out, not_19_out, not_20_out, not_21_out, not_22_out,
       not_23_out, not_24_out;
  wire [7:7] or_2_out;

  nor nor_1 (nor_1_out, funct[3], funct[4], funct[5]);
  not not_1 (not_1_out, funct[5]);
  not not_2 (not_2_out, funct[4]);
  and and_1 (controls[16], not_1_out, not_2_out, funct[3], not_3_out, not_4_out, funct[0]);
  not not_3 (not_3_out, funct[2]);
  not not_4 (not_4_out, funct[1]);
  not not_5 (not_5_out, funct[5]);
  not not_6 (not_6_out, funct[4]);
  and and_2 (and_2_out, not_5_out, not_6_out, funct[3], not_7_out, not_8_out, not_9_out);
  not not_7 (not_7_out, funct[2]);
  not not_8 (not_8_out, funct[1]);
  not not_9 (not_9_out, funct[0]);
  not not_10 (controls[4], funct[4]);
  not not_11 (not_11_out, funct[2]);
  not not_12 (not_12_out, funct[4]);
  not not_13 (not_13_out, funct[5]);
  not not_14 (not_14_out, funct[0]);
  not not_15 (not_15_out, funct[2]);
  and and_3 (and_3_out, funct[0], funct[1], not_16_out);
  not not_16 (not_16_out, funct[2]);
  not not_17 (not_17_out, funct[4]);
  and and_4 (and_4_out, funct[3], not_17_out, funct[5]);
  and and_5 (and_5_out, funct[0], funct[1], not_11_out);
  and and_6 (controls[8], and_5_out, and_7_out);
  and and_7 (and_7_out, funct[3], not_12_out, not_13_out);
  and and_8 (and_8_out, not_14_out, funct[1], not_15_out);
  and and_9 (controls[9], funct[2], nor_1_out);
  and and_10 (controls[10], and_3_out, and_4_out);
  or or_1 (controls[15], controls[16], and_2_out);
  not not_18 (not_18_out, funct[5]);
  not not_19 (not_19_out, funct[3]);
  not not_20 (not_20_out, funct[5]);
  not not_21 (not_21_out, funct[3]);
  not not_22 (not_22_out, funct[5]);
  not not_23 (not_23_out, funct[5]);
  not not_24 (not_24_out, funct[3]);
  not not_25 (controls[6], funct[3]);
  and and_11 (and_11_out, and_7_out, and_8_out);
  and and_12 (and_12_out, not_18_out, funct[3]);
  and and_13 (and_13_out, funct[5], funct[2]);
  and and_14 (controls[2], not_19_out, funct[1]);
  and and_15 (and_15_out, not_20_out, funct[3]);
  and and_16 (and_16_out, funct[5], not_21_out, funct[0]);
  and and_17 (and_17_out, not_22_out, funct[0]);
  and and_18 (and_18_out, not_23_out, funct[3]);
  or or_2 (or_2_out[7], not_24_out, funct[1]);
  or or_3 (controls[3], and_12_out, and_13_out);
  or or_4 (controls[1], and_15_out, and_16_out);
  or or_5 (controls[0], and_17_out, and_18_out);
  or or_6 (controls[7], controls[8], and_11_out);

  assign {controls[17], controls[14:11], controls[5]} = {6{funct[4]}};
  assign j = controls[15];
  assign up31 = controls[16];
endmodule

module MEWB (
  input  [31:0] C,
  input  [4:0] rd,
  input  regWrt,
  input  [31:0] MemD,
  input  MemtoReg,
  input  Clk,
  output [31:0] CO,
  output [4:0] rdO,
  output regWrtO,
  output [31:0] MemDO,
  output MemtoRegO
);

  Register #(.width(32)) register_1 (.D(C), .clk(Clk), .Q(CO));  // open: en, clr
  Register #(.width(5)) register_2 (.D(rd), .clk(Clk), .Q(rdO));  // open: en, clr
  Register #(.width(1)) register_3 (.D(regWrt), .clk(Clk), .Q(regWrtO));  // open: en, clr
  Register #(.width(32)) register_4 (.D(MemD), .clk(Clk), .Q(MemDO));  // open: en, clr
  Register #(.width(1)) register_5 (.D(MemtoReg), .clk(Clk), .Q(MemtoRegO));  // open: en, clr
endmodule

module ExHazards (
  input  EM_regWr,
  input  [4:0] EM_rd,
  input  [4:0] IE_rs,
  input  [4:0] IE_rt,
  output [1:0] ForwardA,
  output [1:0] ForwardB
);

  wire equal_1_cout, equal_2_cout, nz_1_c;
  wire [1:0] bit_extender_1_out, bit_extender_2_out;
  wire [1:1] and_1_out, and_2_out;

  nz nz_1 (.rv(EM_rd), .C(nz_1_c));
  equal equal_1 (.inpOne(EM_rd), .inpTwo(IE_rs), .Cout(equal_1_cout));
  equal equal_2 (.inpOne(EM_rd), .inpTwo(IE_rt), .Cout(equal_2_cout));
  and and_1 (and_1_out[1], EM_regWr, nz_1_c, equal_1_cout);
  and and_2 (and_2_out[1], equal_2_cout, nz_1_c, EM_regWr);
  assign bit_extender_1_out = {{1{1'b0}}, and_1_out[1]};  // Bit_Extender bit_extender_1
  assign bit_extender_2_out = {{1{1'b0}}, and_2_out[1]};  // Bit_Extender bit_extender_2
  Multiplexer #(.width(2), .enable("false")) multiplexer_1 (
    .in0(bit_extender_1_out), .in1({and_1_out[1], bit_extender_1_out[1]}), .out(ForwardA), .sel(and_1_out[1]));
  Multiplexer #(.width(2), .enable("false")) multiplexer_2 (
    .in0(bit_extender_2_out), .in1({and_2_out[1], bit_extender_2_out[1]}), .out(ForwardB), .sel(and_2_out[1]));
endmodule

module MemHazards (
  input  MW_RgW,
  input  EM_RgW,
  input  [4:0] EM_rd,
  input  [4:0] MW_rd,
  input  [4:0] IE_rt,
  input  [4:0] IE_rs,
  output [1:0] ForwardA,
  output [1:0] ForwardB
);

  wire equal_1_cout, equal_2_cout, not_1_out, not_2_out, nz_1_c;
  wire [0:0] and_1_out, and_2_out;
  wire [1:0] bit_extender_1_out, bit_extender_2_out, exhazards_1_forwarda, exhazards_1_forwardb;

  nz nz_1 (.rv(MW_rd), .C(nz_1_c));
  equal equal_1 (.inpOne(MW_rd), .inpTwo(IE_rs), .Cout(equal_1_cout));
  ExHazards exhazards_1 (
    .EM_regWr(EM_RgW), .EM_rd(EM_rd), .IE_rs(IE_rs), .IE_rt(IE_rt), .ForwardA(exhazards_1_forwarda),
    .ForwardB(exhazards_1_forwardb));
  not not_1 (not_1_out, exhazards_1_forwarda[1]);
  not not_2 (not_2_out, exhazards_1_forwardb[1]);
  equal equal_2 (.inpOne(MW_rd), .inpTwo(IE_rt), .Cout(equal_2_cout));
  and and_1 (and_1_out[0], equal_1_cout, MW_RgW, nz_1_c, not_1_out);
  and and_2 (and_2_out[0], not_2_out, MW_RgW, nz_1_c, equal_2_cout);
  assign bit_extender_1_out = {{1{1'b0}}, and_1_out[0]};  // Bit_Extender bit_extender_1
  assign bit_extender_2_out = {{1{1'b0}}, and_2_out[0]};  // Bit_Extender bit_extender_2
  Multiplexer #(.width(2), .enable("false")) multiplexer_1 (
    .in0(bit_extender_1_out), .in1({bit_extender_1_out[1], and_1_out[0]}), .out(ForwardA), .sel(and_1_out[0]));
  Multiplexer #(.width(2), .enable("false")) multiplexer_2 (
    .in0(bit_extender_2_out), .in1({bit_extender_2_out[1], and_2_out[0]}), .out(ForwardB), .sel(and_2_out[0]));
endmodule

module ForwardingUnit (
  input  EM_regWr,
  input  [4:0] EM_rd,
  input  [4:0] IE_rs,
  input  [4:0] IE_rt,
  input  MW_regWr,
  input  [4:0] MW_rd,
  output [1:0] ForwardA,
  output [1:0] ForwardB
);

  wire [1:0] exhazards_1_forwarda, exhazards_1_forwardb, memhazards_1_forwarda, memhazards_1_forwardb;

  ExHazards exhazards_1 (
    .EM_regWr(EM_regWr), .EM_rd(EM_rd), .IE_rs(IE_rs), .IE_rt(IE_rt), .ForwardA(exhazards_1_forwarda),
    .ForwardB(exhazards_1_forwardb));
  MemHazards memhazards_1 (
    .MW_RgW(MW_regWr), .EM_RgW(EM_regWr), .EM_rd(EM_rd), .MW_rd(MW_rd), .IE_rt(IE_rt), .IE_rs(IE_rs),
    .ForwardA(memhazards_1_forwarda), .ForwardB(memhazards_1_forwardb));
  Multiplexer #(.width(2), .enable("false")) multiplexer_1 (
    .in0(memhazards_1_forwarda), .in1(exhazards_1_forwarda), .out(ForwardA), .sel(exhazards_1_forwarda[1]));
  Multiplexer #(.width(2), .enable("false")) multiplexer_2 (
    .in0(memhazards_1_forwardb), .in1(exhazards_1_forwardb), .out(ForwardB), .sel(exhazards_1_forwardb[1]));
endmodule

module equal (
  input  [4:0] inpOne,
  input  [4:0] inpTwo,
  output Cout
);

  wire not_1_out, not_2_out, not_3_out, not_4_out, not_5_out, xor_1_out, xor_2_out, xor_3_out, xor_4_out,
       xor_5_out;

  not not_1 (not_1_out, xor_1_out);
  xor xor_1 (xor_1_out, inpOne[0], inpTwo[0]);
  not not_2 (not_2_out, xor_2_out);
  xor xor_2 (xor_2_out, inpOne[1], inpTwo[1]);
  xor xor_3 (xor_3_out, inpOne[2], inpTwo[2]);
  not not_3 (not_3_out, xor_3_out);
  xor xor_4 (xor_4_out, inpOne[3], inpTwo[3]);
  not not_4 (not_4_out, xor_4_out);
  not not_5 (not_5_out, xor_5_out);
  xor xor_5 (xor_5_out, inpOne[4], inpTwo[4]);
  and and_1 (Cout, not_1_out, not_2_out, not_3_out, not_4_out, not_5_out);
endmodule

module nz (
  input  [4:0] rv,
  output C
);

  wire and_1_out;
  wire [4:0] not_1_out;

  assign not_1_out = ~rv;  // NOT_Gate not_1, 5 bits wide
  and and_1 (and_1_out, not_1_out[0], not_1_out[1], not_1_out[2], not_1_out[3], not_1_out[4]);
  not not_2 (C, and_1_out);
endmodule

module JDecode (
  input  [5:0] op,
  output [17:0] controls,
  output j,
  output up31
);

  wire and_2_out, not_1_out, not_2_out, not_3_out, not_4_out, not_5_out, not_6_out, not_7_out, not_8_out,
       not_9_out;

  not not_1 (not_1_out, op[2]);
  not not_2 (not_2_out, op[3]);
  not not_3 (not_3_out, op[4]);
  not not_4 (not_4_out, op[5]);
  not not_5 (not_5_out, op[0]);
  not not_6 (not_6_out, op[2]);
  not not_7 (not_7_out, op[3]);
  not not_8 (not_8_out, op[4]);
  not not_9 (not_9_out, op[5]);
  and and_1 (controls[16], op[0], op[1], not_1_out, not_2_out, not_3_out, not_4_out);
  and and_2 (and_2_out, not_5_out, op[1], not_6_out, not_7_out, not_8_out, not_9_out);
  or or_1 (controls[15], controls[16], and_2_out);

  assign {controls[17], controls[14:0]} = {16{op[4]}};
  assign j = controls[15];
  assign up31 = controls[16];
endmodule

module Branch (
  input  [31:0] instr,
  output branch,
  output [6:0] b_op
);

  wire and_1_out, and_2_out, and_3_out, and_4_out, and_5_out, and_6_out, and_7_out, and_8_out, and_9_out,
       not_1_out, not_2_out, not_3_out, not_4_out, not_5_out, not_6_out, not_7_out, not_8_out, not_9_out,
       not_10_out, not_11_out, not_12_out, not_13_out, not_14_out, or_1_out, or_2_out;

  or or_1 (or_1_out, instr[31], instr[30], instr[29], instr[28], instr[27], instr[26]);
  not not_1 (not_1_out, instr[31]);
  not not_2 (not_2_out, instr[30]);
  and and_1 (and_1_out, not_1_out, not_2_out, not_3_out);
  not not_3 (not_3_out, instr[29]);
  not not_4 (not_4_out, instr[27]);
  and and_2 (and_2_out, instr[28], not_4_out, not_5_out);
  not not_5 (not_5_out, instr[26]);
  not not_6 (not_6_out, instr[27]);
  and and_3 (and_3_out, instr[28], not_6_out, instr[26]);
  and and_4 (and_4_out, instr[28], instr[27], not_7_out);
  not not_7 (not_7_out, instr[26]);
  and and_5 (and_5_out, instr[28], instr[27], instr[26]);
  not not_8 (not_8_out, instr[28]);
  and and_6 (and_6_out, not_8_out, not_9_out, instr[26]);
  not not_9 (not_9_out, instr[27]);
  not not_10 (not_10_out, instr[20]);
  not not_11 (not_11_out, instr[19]);
  and and_7 (and_7_out, not_10_out, not_11_out, not_12_out, not_13_out);
  not not_12 (not_12_out, instr[18]);
  not not_13 (not_13_out, instr[17]);
  not not_14 (not_14_out, instr[16]);
  and and_8 (and_8_out, and_7_out, not_14_out);
  and and_9 (and_9_out, and_7_out, instr[16]);
  and and_10 (b_op[0], and_1_out, and_2_out);
  and and_11 (b_op[1], and_1_out, and_3_out);
  and and_12 (b_op[2], and_1_out, and_4_out);
  and and_13 (b_op[3], and_1_out, and_5_out);
  and and_14 (b_op[4], and_6_out, and_1_out, and_8_out);
  and and_15 (b_op[5], and_6_out, and_1_out, and_9_out);
  or or_2 (or_2_out, b_op[0], b_op[1], b_op[2], b_op[3], b_op[4], b_op[5]);
  and and_16 (branch, or_1_out, or_2_out, and_1_out);

  assign b_op[6] = instr[30];
endmodule

module MemDecode (
  input  [5:0] op,
  output ALU3,
  output ALU2,
  output ALU1,
  output ALU0,
  output RegDst,
  output ALUSrc,
  output MemtoReg,
  output RegWrite,
  output MemRead,
  output MemWrite,
  output ALUOut,
  output unsigLB,
  output isWord
);

  wire and_2_out, and_3_out, not_1_out, not_2_out, not_3_out, not_4_out, not_5_out, not_6_out, not_7_out,
       not_8_out, not_9_out, not_11_out, not_12_out, not_13_out;

  not not_1 (not_1_out, op[4]);
  not not_2 (not_2_out, op[3]);
  not not_3 (not_3_out, op[1]);
  not not_4 (not_4_out, op[0]);
  not not_5 (not_5_out, op[4]);
  not not_6 (not_6_out, op[3]);
  not not_7 (not_7_out, op[2]);
  not not_8 (not_8_out, op[4]);
  not not_9 (not_9_out, op[2]);
  not not_10 (ALU1, op[4]);
  and and_1 (unsigLB, op[5], not_1_out, not_2_out, op[2], not_3_out, not_4_out);
  and and_2 (and_2_out, op[5], not_5_out, not_6_out, not_7_out, op[1], op[0]);
  and and_3 (and_3_out, op[5], not_8_out, op[3], not_9_out, op[1], op[0]);
  and and_4 (MemtoReg, op[5], not_11_out);
  not not_11 (not_11_out, op[3]);
  and and_5 (RegWrite, op[5], not_12_out);
  not not_12 (not_12_out, op[3]);
  and and_6 (MemRead, op[5], not_13_out);
  not not_13 (not_13_out, op[3]);
  and and_7 (MemWrite, op[5], op[3]);
  or or_1 (isWord, and_2_out, and_3_out);

  assign ALU0 = op[4];
  assign ALU2 = op[4];
  assign ALU3 = op[4];
  assign ALUOut = ALU1;
  assign ALUSrc = ALU1;
  assign RegDst = op[4];
endmodule

module branchCmpt (
  input  [17:0] controls,
  input  [31:0] rs,
  input  [6:0] br_op,
  input  [31:0] rt,
  output br
);

  wire and_1_out, and_2_out, and_3_out, and_4_out, and_5_out, and_6_out, comparator_1_eq, comparator_1_gt,
       comparator_1_lt, not_1_out, or_1_out, or_2_out, or_3_out, or_4_out;
  wire [31:0] bit_extender_1_out, multiplexer_1_out;

  or or_1 (or_1_out, br_op[0], br_op[1]);
  assign bit_extender_1_out = {{31{1'b0}}, br_op[6]};  // Bit_Extender bit_extender_1
  Multiplexer #(.width(32), .enable("false")) multiplexer_1 (
    .in0(bit_extender_1_out), .in1(rt), .out(multiplexer_1_out), .sel(or_1_out));
  Comparator #(.width(32)) comparator_1 (
    .a(rs), .b(multiplexer_1_out), .gt(comparator_1_gt), .eq(comparator_1_eq), .lt(comparator_1_lt));
  not not_1 (not_1_out, comparator_1_eq);
  or or_2 (or_2_out, comparator_1_eq, comparator_1_lt);
  or or_3 (or_3_out, comparator_1_eq, comparator_1_gt);
  and and_1 (and_1_out, br_op[0], comparator_1_eq);
  and and_2 (and_2_out, br_op[1], not_1_out);
  and and_3 (and_3_out, br_op[2], or_2_out);
  and and_4 (and_4_out, comparator_1_gt, br_op[3]);
  and and_5 (and_5_out, comparator_1_lt, br_op[4]);
  and and_6 (and_6_out, or_3_out, br_op[5]);
  or or_4 (or_4_out, and_1_out, and_2_out, and_3_out, and_4_out, and_5_out, and_6_out);
  and and_7 (br, controls[17], or_4_out);
endmodule

module Fetch (
  input  jump,
  input  Stall,
  input  [31:0] jumpT,
  input  Clk,
  input  bt,
  input  [31:0] b_target,
  output [31:0] Addr
);

  wire not_1_out;
  wire [31:0] incrementer_1_p2, multiplexer_1_out, multiplexer_2_out;

  Multiplexer #(.width(32), .enable("false")) multiplexer_1 (
    .in0({incrementer_1_p2[29:0], {2{Addr[1]}}}), .in1(b_target), .out(multiplexer_1_out), .sel(bt));
  Multiplexer #(.width(32), .enable("false")) multiplexer_2 (
    .in0(multiplexer_1_out), .in1(jumpT), .out(multiplexer_2_out), .sel(jump));
  Register #(.width(32)) PC (.D(multiplexer_2_out), .en(not_1_out), .clk(Clk), .Q(Addr));  // open: clr
  not not_1 (not_1_out, Stall);
  // Incrementer #(.width(32)) incrementer_1: pin names not known; wires that end beside it: {{2{Addr[1]}}, Addr[31:2]}, incrementer_1_p2
endmodule

module shifttwo (
  input  z,
  input  [31:0] imm,
  output [31:0] out_3
);


  assign out_3 = {imm[29:0], {2{z}}};
endmodule

module plusfour (
  input  [31:0] PC,
  output [31:0] PCFour
);

  wire [31:30] incrementer_1_p2;

  // Incrementer #(.width(32)) incrementer_1: pin names not known; wires that end beside it: {{2{PC[1]}}, PC[31:2]}, {incrementer_1_p2, PCFour[31:2]}

  assign PCFour[1:0] = {2{PC[1]}};
endmodule

module jumpCmpt (
  input  [17:0] controls,
  input  jtype,
  input  [25:0] target,
  input  [31:0] plusfour,
  input  [31:0] rs,
  output [31:0] newpc
);

  wire and_1_out, not_1_out;
  wire [27:0] bit_extender_1_out;

  not not_1 (not_1_out, jtype);
  assign bit_extender_1_out = {{2{1'b0}}, target};  // Bit_Extender bit_extender_1
  and and_1 (and_1_out, controls[15], not_1_out);
  Multiplexer #(.width(32), .enable("false")) multiplexer_1 (
    .in0({plusfour[31:28], bit_extender_1_out[25:0], {2{controls[11]}}}), .in1(rs), .out(newpc),
    .sel(and_1_out));
endmodule

module MemCmp (
  input  [31:0] C,
  input  [31:0] Addr,
  input  isWord,
  input  MemW,
  output [31:0] D,
  output [1:0] Re,
  output [3:0] sel,
  output [23:0] A,
  output MemWO
);

  wire not_1_out, or_1_out;
  wire [3:0] and_4_out, bit_extender_1_out;
  wire [31:0] shifter_1_out;

  or or_1 (or_1_out, Addr[31], Addr[30], Addr[29], Addr[28], Addr[27], Addr[26]);
  not not_1 (not_1_out, or_1_out);
  and and_1 (and_4_out[3], Addr[0], Addr[1]);
  and and_2 (and_4_out[2], ~Addr[0], Addr[1]);  // AND_Gate
  and and_3 (and_4_out[1], Addr[0], ~Addr[1]);  // AND_Gate
  and and_4 (and_4_out[0], ~Addr[0], ~Addr[1]);  // AND_Gate
  Multiplexer #(.width(24), .enable("false")) multiplexer_1 (.in0(Addr[23:0]), .in1(Addr[23:0]), .out(A), .sel(isWord));
  Multiplexer #(.enable("false")) multiplexer_2 (.in0(MemW), .in1(not_1_out), .out(MemWO), .sel(or_1_out));
  Shifter #(.width(32)) shifter_1 (.in(C), .\dist ({Addr[1:0], {3{isWord}}}), .out(shifter_1_out));
  assign bit_extender_1_out = {{3{isWord}}, isWord};  // Bit_Extender bit_extender_1
  Multiplexer #(.width(32), .enable("false")) multiplexer_3 (.in0(shifter_1_out), .in1(C), .out(D), .sel(isWord));
  Multiplexer #(.width(4), .enable("false")) multiplexer_4 (
    .in0(and_4_out), .in1(bit_extender_1_out), .out(sel), .sel(isWord));

  assign Re = Addr[1:0];
endmodule

module LoadStall (
  input  EX_memR,
  input  [4:0] ID_rs,
  input  [4:0] EX_rd,
  input  [4:0] ID_rt,
  output stall
);

  wire equal_1_cout, equal_2_cout, or_1_out;

  equal equal_1 (.inpOne(ID_rs), .inpTwo(EX_rd), .Cout(equal_1_cout));
  equal equal_2 (.inpOne(EX_rd), .inpTwo(ID_rt), .Cout(equal_2_cout));
  or or_1 (or_1_out, equal_1_cout, equal_2_cout);
  and and_1 (stall, EX_memR, or_1_out);
endmodule

module nopC (
  input  zIn,
  output [17:0] nopC
);

  not not_1 (nopC[4], zIn);
  not not_2 (nopC[6], zIn);

  assign {nopC[17:7], nopC[5], nopC[3:0]} = {16{zIn}};
endmodule
