// Logisim project pp1_proj.circ as structural Verilog: 15 circuits, main circuit MIPS32
module MIPS32 (
);

  wire clock_1_out, decode_1_regwr, decode_1_sig, execute_1_regwro, exme_1_memtorego, exme_1_regwro,
       idex_1_regwro, not_1_out, registerfile_1_p3;
  wire [1:0] forwardingunit_1_forwarda, forwardingunit_1_forwardb;
  wire [4:0] bit_extender_1_out, exme_1_rdo, idex_1_rdo, idex_1_rso, idex_1_rto, idex_1_shamto,
       ifid_1_instrout_2, ifid_1_instrout_3, multiplexer_2_out, multiplexer_3_out, registerfile_1_p4;
  wire [14:0] decode_1_controls, idex_1_conto;
  wire [31:0] bit_extender_2_out, bit_extender_3_out, execute_1_c, exme_1_co, fetch_1_addr, idex_1_ao,
       idex_1_bo, idex_1_immo, ifid_1_instrout, mipsprogramrom_1_p3, multiplexer_1_out, registerfile_1_p1,
       registerfile_1_p7, registerfile_1_p8;

  Clock clock_1 (.out(clock_1_out));
  Fetch fetch_1 (.Addr(fetch_1_addr), .Clk(clock_1_out));
  // MIPSProgramROM mipsprogramrom_1: pin names not known; wires that end beside it: clock_1_out, fetch_1_addr, mipsprogramrom_1_p3
  IFID ifid_1 (
    .instrOut({ifid_1_instrout[31:26], ifid_1_instrout_3, ifid_1_instrout[20:11], ifid_1_instrout_2, ifid_1_instrout[5:0]}),
    .instrIn(mipsprogramrom_1_p3), .Clk(clock_1_out));
  not not_1 (not_1_out, clock_1_out);
  assign bit_extender_1_out = {{4{1'b0}}, ifid_1_instrout[30]};  // Bit_Extender bit_extender_1
  assign bit_extender_2_out = {{16{ifid_1_instrout[15]}}, {ifid_1_instrout[15:11], ifid_1_instrout_2, ifid_1_instrout[5:0]}};  // Bit_Extender bit_extender_2
  assign bit_extender_3_out = {{16{1'b0}}, {ifid_1_instrout[15:11], ifid_1_instrout_2, ifid_1_instrout[5:0]}};  // Bit_Extender bit_extender_3
  Multiplexer #(.width(32), .enable("false")) multiplexer_1 (
    .in0(bit_extender_2_out), .in1(bit_extender_3_out), .out(multiplexer_1_out), .sel(decode_1_sig));
  // RegisterFile registerfile_1: pin names not known; wires that end beside it: registerfile_1_p1, not_1_out, registerfile_1_p3, registerfile_1_p4, ifid_1_instrout_3, ifid_1_instrout[20:16], registerfile_1_p7, registerfile_1_p8
  Decode decode_1 (
    .instr({ifid_1_instrout[31:26], ifid_1_instrout_3, ifid_1_instrout[20:11], ifid_1_instrout_2, ifid_1_instrout[5:0]}),
    .controls(decode_1_controls), .regWr(decode_1_regwr), .sig(decode_1_sig));
  Multiplexer #(.width(5), .enable("false")) multiplexer_2 (
    .in0(ifid_1_instrout[20:16]), .in1(ifid_1_instrout[15:11]), .out(multiplexer_2_out),
    .sel(decode_1_controls[4]));
  Multiplexer #(.width(5), .enable("false")) multiplexer_3 (
    .in0(bit_extender_1_out), .in1(ifid_1_instrout[20:16]), .out(multiplexer_3_out),
    .sel(decode_1_controls[4]));
  IDEX idex_1 (
    .A(registerfile_1_p7), .AO(idex_1_ao), .B(registerfile_1_p8), .BO(idex_1_bo), .Clk(clock_1_out),
    .rd(multiplexer_2_out), .rdO(idex_1_rdo), .rt(multiplexer_3_out), .rtO(idex_1_rto),
    .shamt(ifid_1_instrout_2), .shamtO(idex_1_shamto), .Imm(multiplexer_1_out), .ImmO(idex_1_immo),
    .rs(ifid_1_instrout_3), .rsO(idex_1_rso), .cont(decode_1_controls), .contO(idex_1_conto),
    .regWrO(idex_1_regwro), .regWr(decode_1_regwr));
  Execute execute_1 (
    .C(execute_1_c), .A(idex_1_ao), .B(idex_1_bo), .imm(idex_1_immo), .shamt(idex_1_shamto),
    .controls(idex_1_conto), .regWrO(execute_1_regwro), .regWr(idex_1_regwro),
    .ForwardA(forwardingunit_1_forwarda), .ForwardB(forwardingunit_1_forwardb), .EXMEMC(exme_1_co),
    .MEMWBC(registerfile_1_p1));
  ForwardingUnit forwardingunit_1 (
    .EM_regWr(exme_1_regwro), .EM_rd(exme_1_rdo), .IE_rs(idex_1_rso), .IE_rt(idex_1_rto),
    .MW_regWr(registerfile_1_p3), .MW_rd(registerfile_1_p4), .ForwardA(forwardingunit_1_forwarda),
    .ForwardB(forwardingunit_1_forwardb));
  EXME exme_1 (
    .MemtoRegO(exme_1_memtorego), .C(execute_1_c), .RegWrO(exme_1_regwro), .rd(idex_1_rdo), .rdO(exme_1_rdo),
    .RegWr(execute_1_regwro), .CO(exme_1_co), .controls(idex_1_conto), .Clk(clock_1_out));  // open: MemReadO, MemWriteO
  MEWB mewb_1 (
    .rdO(registerfile_1_p4), .Clk(clock_1_out), .regWrt(exme_1_regwro), .MemtoReg(exme_1_memtorego),
    .CO(registerfile_1_p1), .rd(exme_1_rdo), .C(exme_1_co), .regWrtO(registerfile_1_p3));  // open: MemtoRegO

  // Notes on the sheet:
  //   contents of mipsprogramrom_1 (hex, n*v repeats v):
  //   addiu $2, $0, 3          addiu $3, $0, 4                 subu $4, $1, $1                 sll $5, $1,
  //   2           sll $6, $2, 2           slt $7, $2, $1         # 1 movz $8, $3, $4             # 4 lui
  //   $9, 1           # 0 movn $10, $3, $2    # 4 movn $10, $1, $4    # 4 xor $11, $1, $2             # 6
  //   xori $12, $3, 4             # 0 xori $12, $3, 5             # 1 sra $6, $6, 2               # 0
  //   addiu $13, $0, -5   # fffffffb subu $14, $2, $1     # fffffffe sra $15, $14, 1              #
  //   ffffffff sra $16, $13, 1              # fffffffd andi $15, $1, 3              # 1 sltu $17, $6, $14
  //   # 1 slti $18, $6, -2    # 0 sltiu $19, $6, -2   # 1 andi $19, $18, 1    # 0 andi $19, $18, 0    # 0
  //   addiu $19, $0, 1    # 1 andi $19, $19, 1    # 1 ori $19, $19, 0             # 1 xori $19, $19, 1
  //   # 0 addu $24, $19, $3   # 4 subu $24, $5, $3    # 11 and $25, $24, $19  # 0 and $26, $3, $7
  //   # 0 and $26, $3, $3             # 4 or $28, $26, $3             # 4 xor $20, $21, $3    # 0 nor $20,
  //   $19, $3    # 1 movz $20, $18, $3            lui $9, 24 lui $9, 23 lui $9, 22 lui $9, 21
  //   movn $10, $3, $2       # 4 movn $10, $1, $4    # 4 movn $10, $3, $20   # 4 movn $10, $5, $4    # 4
  //   movn $10, $8, $2    # 4 movn $10, $7, $4    # 4 movn $10, $3, $2    # 4 movn $10, $1, $4    # 4 movn
  //   $10, $4, $2    # 4 movn $10, $4, $7    # 4 movn $10, $2, $2    # 4 movn $10, $1, $0    # 4 xor $11,
  //   $1, $2             # 6 xori $12, $3, 4             # 0 xori $12, $3, 5             # 1 sra $6, $6, 2
  //   # 0 addiu $13, $0, -5   # fffffffb xori $12, $3, 5              # 1 sra $6, $6, 2               # 0
  //   addiu $10, $0, -5   # fffffffb subu $14, $2, $1     # fffffffe sra $15, $14, 1              #
  //   ffffffff sra $16, $13, 1              # fffffffd andi $15, $1, 3              # 1 sltu $17, $6, $14
  //   # 1 slti $18, $6, -2    # 0 sltiu $19, $6, -2   # 1
endmodule

module Fetch (
  input  Clk,
  output [31:0] Addr
);

  wire [31:0] incrementer_1_p2;

  Register #(.width(32)) PC (.D({incrementer_1_p2[29:0], {2{Addr[1]}}}), .clk(Clk), .Q(Addr));  // open: en, clr
  // Incrementer #(.width(32)) incrementer_1: pin names not known; wires that end beside it: {{2{Addr[1]}}, Addr[31:2]}, incrementer_1_p2
endmodule

module IFID (
  input  [31:0] instrIn,
  input  Clk,
  output [31:0] instrOut
);

  Register #(.width(32)) register_1 (.D(instrIn), .clk(Clk), .Q(instrOut));  // open: en, clr
endmodule

module IDecode (
  input  [5:0] op,
  output ALU3,
  output ALU2,
  output ALU1,
  output ALU0,
  output RegDst,
  output ALUSrc,
  output MemtoReg,
  output RegWrite,
  output MemRead,
  output MemWrite,
  output ALUOut
);

  wire and_1_out, and_2_out, and_3_out, and_4_out, and_5_out, and_6_out, and_7_out, and_8_out, not_1_out,
       not_2_out, not_3_out, not_4_out, not_5_out, not_6_out, not_7_out, not_8_out, not_9_out, not_10_out,
       not_11_out, not_12_out, not_13_out, not_14_out, not_15_out, not_16_out, not_17_out, not_18_out;

  not not_1 (not_1_out, op[5]);
  not not_2 (not_2_out, op[3]);
  not not_3 (not_3_out, op[2]);
  not not_4 (not_4_out, op[0]);
  not not_5 (not_5_out, op[5]);
  not not_6 (not_6_out, op[3]);
  not not_7 (not_7_out, op[5]);
  not not_8 (not_8_out, op[2]);
  not not_9 (not_9_out, op[0]);
  not not_10 (not_10_out, op[3]);
  not not_11 (not_11_out, op[1]);
  not not_12 (not_12_out, op[1]);
  not not_13 (not_13_out, op[5]);
  not not_14 (not_14_out, op[1]);
  and and_1 (and_1_out, not_1_out, not_2_out, not_3_out, not_4_out);
  and and_2 (and_2_out, op[3], op[2], not_15_out);
  not not_15 (not_15_out, op[1]);
  and and_3 (and_3_out, op[3], op[2], not_16_out);
  not not_16 (not_16_out, op[0]);
  and and_4 (and_4_out, not_5_out, not_6_out);
  and and_5 (and_5_out, not_7_out, not_8_out, op[1]);
  and and_6 (and_6_out, op[1], not_9_out);
  and and_7 (and_7_out, not_10_out, op[2], op[1]);
  not not_17 (not_17_out, op[3]);
  not not_18 (not_18_out, op[2]);
  and and_8 (and_8_out, not_11_out, op[0]);
  or or_1 (ALUSrc, not_12_out, op[2], op[3], op[5]);
  and and_9 (RegWrite, not_13_out, op[3]);
  or or_2 (ALUOut, not_14_out, op[2], op[5]);
  or or_3 (ALU3, and_1_out, and_2_out, and_3_out);
  or or_4 (ALU2, and_4_out, and_5_out, and_6_out, and_7_out);
  or or_5 (ALU1, not_17_out, not_18_out, and_8_out);

  assign ALU0 = op[5];
  assign MemRead = op[4];
  assign MemtoReg = op[4];
  assign MemWrite = op[4];
  assign RegDst = op[4];
endmodule

module Decode (
  input  [31:0] instr,
  output [14:0] controls,
  output regWr,
  output sig
);

  wire and_1_out, and_2_out, and_3_out, and_4_out, and_5_out, and_9_out, and_11_out, nand_1_out, nor_1_out,
       nor_2_out, not_1_out, not_2_out, not_3_out, not_4_out, not_5_out, not_6_out, not_7_out, not_8_out;
  wire [10:0] idecode_1_alu3, rdecode_1_alu3;

  not not_1 (not_1_out, instr[2]);
  not not_2 (not_2_out, instr[4]);
  nor nor_1 (nor_1_out, instr[3], instr[4], instr[5]);
  and and_1 (and_1_out, instr[0], instr[1], not_1_out, instr[3], not_2_out, instr[5]);
  and and_2 (and_2_out, instr[0], instr[1], not_3_out);
  not not_3 (not_3_out, instr[2]);
  not not_4 (not_4_out, instr[4]);
  and and_3 (and_3_out, instr[3], not_4_out, not_5_out);
  not not_5 (not_5_out, instr[5]);
  not not_6 (not_6_out, instr[0]);
  and and_4 (and_4_out, not_6_out, instr[1], not_7_out);
  not not_7 (not_7_out, instr[2]);
  nor nor_2 (nor_2_out, instr[26], instr[27], instr[28], instr[29], instr[30], instr[31]);
  and and_5 (and_5_out, instr[26], instr[27], instr[28], instr[29]);
  nand nand_1 (nand_1_out, instr[30], instr[31]);
  not not_8 (not_8_out, instr[28]);
  and and_6 (controls[8], and_2_out, and_3_out);
  and and_7 (controls[9], instr[2], nor_1_out, nor_2_out);
  and and_8 (controls[11], and_5_out, nand_1_out);
  and and_9 (and_9_out, instr[26], instr[27], nand_1_out, not_8_out, instr[29]);
  and and_10 (sig, instr[28], instr[29]);
  and and_11 (and_11_out, and_3_out, and_4_out);
  IDecode idecode_1 (
    .op(instr[31:26]), .ALU3(idecode_1_alu3[0]), .ALU2(idecode_1_alu3[1]), .ALU1(idecode_1_alu3[2]),
    .ALU0(idecode_1_alu3[3]), .RegDst(idecode_1_alu3[4]), .ALUSrc(idecode_1_alu3[5]),
    .MemtoReg(idecode_1_alu3[6]), .RegWrite(idecode_1_alu3[7]), .MemRead(idecode_1_alu3[8]),
    .MemWrite(idecode_1_alu3[9]), .ALUOut(idecode_1_alu3[10]));
  RDecode rdecode_1 (
    .funct(instr[5:0]), .ALU3(rdecode_1_alu3[0]), .ALU2(rdecode_1_alu3[1]), .ALU1(rdecode_1_alu3[2]),
    .ALU0(rdecode_1_alu3[3]), .RegDst(rdecode_1_alu3[4]), .ALUSrc(rdecode_1_alu3[5]),
    .MemtoReg(rdecode_1_alu3[6]), .RegWrite(rdecode_1_alu3[7]), .MemRead(rdecode_1_alu3[8]),
    .MemWrite(rdecode_1_alu3[9]), .ALUOut(rdecode_1_alu3[10]));
  or or_1 (controls[7], controls[8], and_11_out);
  Multiplexer #(.width(11), .enable("false")) multiplexer_1 (
    .in0(idecode_1_alu3), .in1(rdecode_1_alu3),
    .out({controls[6], controls[14:13], regWr, controls[12], controls[5:4], controls[0], controls[1], controls[2], controls[3]}),
    .sel(nor_2_out));
  or or_2 (controls[10], and_1_out, and_9_out);
endmodule

module IDEX (
  input  [31:0] A,
  input  [31:0] B,
  input  [4:0] rd,
  input  [4:0] rt,
  input  [4:0] shamt,
  input  [31:0] Imm,
  input  [4:0] rs,
  input  [14:0] cont,
  input  regWr,
  input  Clk,
  output [31:0] AO,
  output [31:0] BO,
  output [4:0] rdO,
  output [4:0] rtO,
  output [4:0] shamtO,
  output [31:0] ImmO,
  output [4:0] rsO,
  output [14:0] contO,
  output regWrO
);

  Register #(.width(32)) register_1 (.D(A), .clk(Clk), .Q(AO));  // open: en, clr
  Register #(.width(32)) register_2 (.D(B), .clk(Clk), .Q(BO));  // open: en, clr
  Register #(.width(5)) register_3 (.D(rd), .clk(Clk), .Q(rdO));  // open: en, clr
  Register #(.width(5)) register_4 (.D(rt), .clk(Clk), .Q(rtO));  // open: en, clr
  Register #(.width(5)) register_5 (.D(shamt), .clk(Clk), .Q(shamtO));  // open: en, clr
  Register #(.width(32)) register_6 (.D(Imm), .clk(Clk), .Q(ImmO));  // open: en, clr
  Register #(.width(5)) register_7 (.D(rs), .clk(Clk), .Q(rsO));  // open: en, clr
  Register #(.width(15)) register_8 (.D(cont), .clk(Clk), .Q(contO));  // open: en, clr
  Register #(.width(1)) register_9 (.D(regWr), .clk(Clk), .Q(regWrO));  // open: en, clr
endmodule

module Execute (
  input  [31:0] A,
  input  [31:0] B,
  input  [31:0] MEMWBC,
  input  [31:0] imm,
  input  [31:0] EXMEMC,
  input  [4:0] shamt,
  input  [1:0] ForwardA,
  input  [1:0] ForwardB,
  input  regWr,
  input  [14:0] controls,
  output [31:0] C,
  output regWrO
);

  wire and_1_out, and_2_out, and_3_out, comparator_1_eq, comparator_1_lt, comparator_2_lt, not_1_out,
       not_2_out, or_1_out, or_2_out;
  wire [4:0] mips_alu_1_p4, multiplexer_4_out;
  wire [31:0] bit_extender_1_out, bit_extender_2_out, bit_extender_3_out, mips_alu_1_p5, multiplexer_1_out,
       multiplexer_2_out, multiplexer_3_out, multiplexer_6_out, multiplexer_7_out, multiplexer_8_out;

  Multiplexer #(.width(32), .enable("false")) multiplexer_1 (
    .in0(B), .in1(imm), .out(multiplexer_1_out), .sel(controls[5]));
  Multiplexer #(.select(2), .width(32), .enable("false")) multiplexer_2 (
    .in0(A), .in1(MEMWBC), .in2(EXMEMC), .out(multiplexer_2_out), .sel(ForwardA));  // open: in3
  Multiplexer #(.select(2), .width(32), .enable("false")) multiplexer_3 (
    .in0(multiplexer_1_out), .in1(MEMWBC), .in2(EXMEMC), .out(multiplexer_3_out), .sel(ForwardB));  // open: in3
  assign bit_extender_1_out = {{31{1'b0}}, controls[12]};  // Bit_Extender bit_extender_1
  Multiplexer #(.width(5), .enable("false")) multiplexer_4 (
    .in0(shamt), .in1(multiplexer_2_out[4:0]), .out(multiplexer_4_out), .sel(controls[9]));
  // Mips_ALU mips_alu_1: pin names not known; wires that end beside it: multiplexer_2_out, multiplexer_3_out, controls[3:0], mips_alu_1_p4, mips_alu_1_p5
  Multiplexer #(.width(5), .enable("false")) multiplexer_5 (
    .in0(multiplexer_4_out), .in1(5'b10000), .out(mips_alu_1_p4), .sel(controls[11]));
  Multiplexer #(.width(32), .enable("false")) multiplexer_6 (
    .in0(multiplexer_2_out), .in1(bit_extender_1_out), .out(multiplexer_6_out), .sel(controls[7]));
  Comparator #(.width(32)) comparator_1 (
    .a(multiplexer_6_out), .b(multiplexer_3_out), .eq(comparator_1_eq), .lt(comparator_1_lt));  // open: gt
  Comparator #(.width(32), .mode("unsigned")) comparator_2 (
    .a(multiplexer_2_out), .b(multiplexer_3_out), .lt(comparator_2_lt));  // open: gt, eq
  assign bit_extender_2_out = {{31{1'b0}}, comparator_2_lt};  // Bit_Extender bit_extender_2
  assign bit_extender_3_out = {{31{1'b0}}, comparator_1_lt};  // Bit_Extender bit_extender_3
  not not_1 (not_1_out, comparator_1_eq);
  not not_2 (not_2_out, controls[8]);
  and and_1 (and_1_out, not_1_out, controls[8]);
  and and_2 (and_2_out, comparator_1_eq, not_2_out);
  Multiplexer #(.width(32), .enable("false")) multiplexer_7 (
    .in0(bit_extender_2_out), .in1(mips_alu_1_p5), .out(multiplexer_7_out), .sel(controls[6]));
  Multiplexer #(.width(32), .enable("false")) multiplexer_8 (
    .in0(bit_extender_3_out), .in1(multiplexer_2_out), .out(multiplexer_8_out), .sel(controls[7]));
  or or_1 (or_1_out, and_1_out, and_2_out);
  Multiplexer #(.enable("false")) multiplexer_9 (.in0(regWr), .in1(and_3_out), .out(regWrO), .sel(controls[7]));
  and and_3 (and_3_out, controls[7], or_1_out);
  Multiplexer #(.width(32), .enable("false")) multiplexer_10 (
    .in0(multiplexer_8_out), .in1(multiplexer_7_out), .out(C), .sel(or_2_out));
  or or_2 (or_2_out, controls[10], controls[6]);
endmodule

module EXME (
  input  [31:0] C,
  input  [4:0] rd,
  input  RegWr,
  input  [14:0] controls,
  input  Clk,
  output [31:0] CO,
  output [4:0] rdO,
  output RegWrO,
  output MemtoRegO,
  output MemReadO,
  output MemWriteO
);

  Register #(.width(32)) register_1 (.D(C), .clk(Clk), .Q(CO));  // open: en, clr
  Register #(.width(5)) register_2 (.D(rd), .clk(Clk), .Q(rdO));  // open: en, clr
  Register #(.width(1)) register_3 (.D(RegWr), .clk(Clk), .Q(RegWrO));  // open: en, clr
  Register #(.width(1)) register_4 (.D(controls[12]), .clk(Clk), .Q(MemtoRegO));  // open: en, clr
  Register #(.width(1)) register_5 (.D(controls[13]), .clk(Clk), .Q(MemReadO));  // open: en, clr
  Register #(.width(1)) register_6 (.D(controls[14]), .clk(Clk), .Q(MemWriteO));  // open: en, clr
endmodule

module RDecode (
  input  [5:0] funct,
  output ALU3,
  output ALU2,
  output ALU1,
  output ALU0,
  output RegDst,
  output ALUSrc,
  output MemtoReg,
  output RegWrite,
  output MemRead,
  output MemWrite,
  output ALUOut
);

  wire and_1_out, and_2_out, and_4_out, and_5_out, and_6_out, and_7_out, not_2_out, not_3_out, not_4_out,
       not_5_out, not_6_out, not_7_out, not_8_out;

  not not_1 (RegDst, funct[4]);
  not not_2 (not_2_out, funct[5]);
  not not_3 (not_3_out, funct[3]);
  not not_4 (not_4_out, funct[5]);
  not not_5 (not_5_out, funct[3]);
  not not_6 (not_6_out, funct[5]);
  not not_7 (not_7_out, funct[5]);
  not not_8 (not_8_out, funct[3]);
  not not_9 (ALUOut, funct[3]);
  and and_1 (and_1_out, not_2_out, funct[3]);
  and and_2 (and_2_out, funct[5], funct[2]);
  and and_3 (ALU2, not_3_out, funct[1]);
  and and_4 (and_4_out, not_4_out, funct[3]);
  and and_5 (and_5_out, funct[5], not_5_out, funct[0]);
  and and_6 (and_6_out, not_6_out, funct[0]);
  and and_7 (and_7_out, not_7_out, funct[3]);
  or or_1 (RegWrite, not_8_out, funct[1]);
  or or_2 (ALU3, and_1_out, and_2_out);
  or or_3 (ALU1, and_4_out, and_5_out);
  or or_4 (ALU0, and_6_out, and_7_out);

  assign ALUSrc = funct[4];
  assign MemRead = funct[4];
  assign MemtoReg = funct[4];
  assign MemWrite = funct[4];
endmodule

module MEWB (
  input  [31:0] C,
  input  [4:0] rd,
  input  regWrt,
  input  MemtoReg,
  input  Clk,
  output [31:0] CO,
  output [4:0] rdO,
  output regWrtO,
  output MemtoRegO
);

  Register #(.width(32)) register_1 (.D(C), .clk(Clk), .Q(CO));  // open: en, clr
  Register #(.width(5)) register_2 (.D(rd), .clk(Clk), .Q(rdO));  // open: en, clr
  Register #(.width(1)) register_3 (.D(regWrt), .clk(Clk), .Q(regWrtO));  // open: en, clr
  Register #(.width(1)) register_4 (.D(MemtoReg), .clk(Clk), .Q(MemtoRegO));  // open: en, clr
endmodule

module ExHazards (
  input  EM_regWr,
  input  [4:0] EM_rd,
  input  [4:0] IE_rs,
  input  [4:0] IE_rt,
  output [1:0] ForwardA,
  output [1:0] ForwardB
);

  wire equal_1_cout, equal_2_cout, nz_1_c;
  wire [1:0] bit_extender_1_out, bit_extender_2_out;
  wire [1:1] and_1_out, and_2_out;

  nz nz_1 (.rv(EM_rd), .C(nz_1_c));
  equal equal_1 (.inpOne(EM_rd), .inpTwo(IE_rs), .Cout(equal_1_cout));
  equal equal_2 (.inpOne(EM_rd), .inpTwo(IE_rt), .Cout(equal_2_cout));
  and and_1 (and_1_out[1], EM_regWr, nz_1_c, equal_1_cout);
  and and_2 (and_2_out[1], equal_2_cout, nz_1_c, EM_regWr);
  assign bit_extender_1_out = {{1{1'b0}}, and_1_out[1]};  // Bit_Extender bit_extender_1
  assign bit_extender_2_out = {{1{1'b0}}, and_2_out[1]};  // Bit_Extender bit_extender_2
  Multiplexer #(.width(2), .enable("false")) multiplexer_1 (
    .in0(bit_extender_1_out), .in1({and_1_out[1], bit_extender_1_out[1]}), .out(ForwardA), .sel(and_1_out[1]));
  Multiplexer #(.width(2), .enable("false")) multiplexer_2 (
    .in0(bit_extender_2_out), .in1({and_2_out[1], bit_extender_2_out[1]}), .out(ForwardB), .sel(and_2_out[1]));
endmodule

module MemHazards (
  input  MW_RgW,
  input  EM_RgW,
  input  [4:0] EM_rd,
  input  [4:0] MW_rd,
  input  [4:0] IE_rt,
  input  [4:0] IE_rs,
  output [1:0] ForwardA,
  output [1:0] ForwardB
);

  wire equal_1_cout, equal_2_cout, not_1_out, not_2_out, nz_1_c;
  wire [0:0] and_1_out, and_2_out;
  wire [1:0] bit_extender_1_out, bit_extender_2_out, exhazards_1_forwarda, exhazards_1_forwardb;

  nz nz_1 (.rv(MW_rd), .C(nz_1_c));
  equal equal_1 (.inpOne(MW_rd), .inpTwo(IE_rs), .Cout(equal_1_cout));
  ExHazards exhazards_1 (
    .EM_regWr(EM_RgW), .EM_rd(EM_rd), .IE_rs(IE_rs), .IE_rt(IE_rt), .ForwardA(exhazards_1_forwarda),
    .ForwardB(exhazards_1_forwardb));
  not not_1 (not_1_out, exhazards_1_forwarda[1]);
  not not_2 (not_2_out, exhazards_1_forwardb[1]);
  equal equal_2 (.inpOne(MW_rd), .inpTwo(IE_rt), .Cout(equal_2_cout));
  and and_1 (and_1_out[0], equal_1_cout, MW_RgW, nz_1_c, not_1_out);
  and and_2 (and_2_out[0], not_2_out, MW_RgW, nz_1_c, equal_2_cout);
  assign bit_extender_1_out = {{1{1'b0}}, and_1_out[0]};  // Bit_Extender bit_extender_1
  assign bit_extender_2_out = {{1{1'b0}}, and_2_out[0]};  // Bit_Extender bit_extender_2
  Multiplexer #(.width(2), .enable("false")) multiplexer_1 (
    .in0(bit_extender_1_out), .in1({bit_extender_1_out[1], and_1_out[0]}), .out(ForwardA), .sel(and_1_out[0]));
  Multiplexer #(.width(2), .enable("false")) multiplexer_2 (
    .in0(bit_extender_2_out), .in1({bit_extender_2_out[1], and_2_out[0]}), .out(ForwardB), .sel(and_2_out[0]));
endmodule

module ForwardingUnit (
  input  EM_regWr,
  input  [4:0] EM_rd,
  input  [4:0] IE_rs,
  input  [4:0] IE_rt,
  input  MW_regWr,
  input  [4:0] MW_rd,
  output [1:0] ForwardA,
  output [1:0] ForwardB
);

  wire [1:0] exhazards_1_forwarda, exhazards_1_forwardb, memhazards_1_forwarda, memhazards_1_forwardb;

  ExHazards exhazards_1 (
    .EM_regWr(EM_regWr), .EM_rd(EM_rd), .IE_rs(IE_rs), .IE_rt(IE_rt), .ForwardA(exhazards_1_forwarda),
    .ForwardB(exhazards_1_forwardb));
  MemHazards memhazards_1 (
    .MW_RgW(MW_regWr), .EM_RgW(EM_regWr), .EM_rd(EM_rd), .MW_rd(MW_rd), .IE_rt(IE_rt), .IE_rs(IE_rs),
    .ForwardA(memhazards_1_forwarda), .ForwardB(memhazards_1_forwardb));
  Multiplexer #(.width(2), .enable("false")) multiplexer_1 (
    .in0(memhazards_1_forwarda), .in1(exhazards_1_forwarda), .out(ForwardA), .sel(exhazards_1_forwarda[1]));
  Multiplexer #(.width(2), .enable("false")) multiplexer_2 (
    .in0(memhazards_1_forwardb), .in1(exhazards_1_forwardb), .out(ForwardB), .sel(exhazards_1_forwardb[1]));
endmodule

module equal (
  input  [4:0] inpOne,
  input  [4:0] inpTwo,
  output Cout
);

  wire not_1_out, not_2_out, not_3_out, not_4_out, not_5_out, xor_1_out, xor_2_out, xor_3_out, xor_4_out,
       xor_5_out;

  not not_1 (not_1_out, xor_1_out);
  xor xor_1 (xor_1_out, inpOne[0], inpTwo[0]);
  not not_2 (not_2_out, xor_2_out);
  xor xor_2 (xor_2_out, inpOne[1], inpTwo[1]);
  not not_3 (not_3_out, xor_3_out);
  xor xor_3 (xor_3_out, inpOne[2], inpTwo[2]);
  not not_4 (not_4_out, xor_4_out);
  xor xor_4 (xor_4_out, inpOne[3], inpTwo[3]);
  not not_5 (not_5_out, xor_5_out);
  xor xor_5 (xor_5_out, inpOne[4], inpTwo[4]);
  and and_1 (Cout, not_1_out, not_2_out, not_3_out, not_4_out, not_5_out);
endmodule

module nz (
  input  [4:0] rv,
  output C
);

  wire and_1_out;
  wire [4:0] not_1_out;

  assign not_1_out = ~rv;  // NOT_Gate not_1, 5 bits wide
  and and_1 (and_1_out, not_1_out[0], not_1_out[1], not_1_out[2], not_1_out[3], not_1_out[4]);
  not not_2 (C, and_1_out);
endmodule
